// Logisim project Cache.circ as structural Verilog: 8 circuits, main circuit main
module main (
  input  EnableTestHalting,
  output [9:0] CorrectCounter,
  output [9:0] HitCounter,
  output [9:0] MissCounter,
  output [9:0] TestNumber,
  output [7:0] ByteRead,
  output [7:0] CorrectByteRead,
  output Halt
);

  wire and_3_out, and_4_out, and_5_out, CLK, CmdIsRead, Correct, CpuRead, CpuWrite, DidContain, HaltTesting,
       MaxItersReached, MemRead, MemWrite, not_1_out, not_2_out, not_4_out, NotDoneTesting, Ok2Count,
       or_1_out, Ready;
  wire [7:0] CpuWriteValue, MemAddress;
  wire [9:0] CpuAddress;
  wire [31:0] Line2Mem, LineFromMem;

  not not_1 (not_1_out, Ready);
  Clock clock_1 (.out(CLK));
  or or_1 (or_1_out, MaxItersReached, Ready);
  Counter #(.width(4), .max('h9)) MaxClocks (
    .load(Ready), .D(4'b0001), .count(not_1_out), .carry(MaxItersReached), .clk(CLK));  // open: Q, clr
  and and_1 (HaltTesting, EnableTestHalting, CmdIsRead, not_2_out);
  not not_2 (not_2_out, Correct);
  not not_3 (NotDoneTesting, Halt);
  Inputs inputs_1 (
    .HaltTesting(HaltTesting), .Ready(or_1_out), .CLK(CLK), .Done(Halt), .Read(CpuRead), .Write(CpuWrite),
    .Address(CpuAddress), .Value(CpuWriteValue), .TestNumber(TestNumber));
  Cache cache_1 (
    .CpuAddress(CpuAddress), .CpuRead(CpuRead), .CpuWrite(CpuWrite), .CpuWriteValue(CpuWriteValue),
    .CLK(CLK), .Ready(Ready), .DidContain(DidContain), .ByteRead(ByteRead), .MemAddress(MemAddress),
    .MemRead(MemRead), .MemWrite(MemWrite), .LineFromMem(LineFromMem), .Line2Mem(Line2Mem));
  // Probe on CpuRead
  // Probe on CpuWrite
  // Probe on CpuAddress
  // Probe on CpuWriteValue
  // Probe on TestNumber
  // Probe on CorrectByteRead
  // Probe on Correct
  // Probe on Ready
  // Probe on DidContain
  // Probe on ByteRead
  // Probe on MemAddress
  // Probe on MemRead
  // Probe on MemWrite
  // Probe on HitCounter
  // Probe on LineFromMem
  // Probe on Line2Mem
  not not_4 (not_4_out, HaltTesting);
  RAM #(.dataWidth(32), .bus("separate")) ram_1 (
    .addr(MemAddress), .din(Line2Mem), .data(LineFromMem), .str(MemWrite), .clk(CLK), .ld(MemRead));  // open: sel, clr
  and and_2 (Ok2Count, Ready, not_4_out, NotDoneTesting);
  and and_3 (and_3_out, Correct, Ok2Count);
  and and_4 (and_4_out, DidContain, Ok2Count);
  and and_5 (and_5_out, MemRead, NotDoneTesting);
  Checker checker_1 (
    .TestNumber(TestNumber), .YourByteRead(ByteRead), .CmdIsRead(CmdIsRead),
    .CorrectByteRead(CorrectByteRead), .Correct(Correct));
  Counter #(.width(10), .max('h3ff)) u_CorrectCounter (
    .count(and_3_out), .Q(CorrectCounter), .clk(CLK));  // open: load, D, carry, clr
  Counter #(.width(10), .max('h3ff)) u_HitCounter (
    .count(and_4_out), .Q(HitCounter), .clk(CLK));  // open: load, D, carry, clr
  Counter #(.width(10), .max('h3ff)) u_MissCounter (
    .count(and_5_out), .Q(MissCounter), .clk(CLK));  // open: load, D, carry, clr
  // Probe on CorrectCounter
  // Probe on HitCounter
  // Probe on MissCounter

  // Other names for the same wires on the sheet: DoneTesting = Halt

  // Notes on the sheet:
  //   Your Answer Inside Here
endmodule

module Cache (
  input  [9:0] CpuAddress,
  input  CpuRead,
  input  CpuWrite,
  input  [7:0] CpuWriteValue,
  input  CLK,
  input  [31:0] LineFromMem,
  output Ready,
  output DidContain,
  output [7:0] ByteRead,
  output [7:0] MemAddress,
  output MemRead,
  output MemWrite,
  output [31:0] Line2Mem
);

  wire enableSet0, enableSet1, setDirty, setValid, updateAge, valid;

  // Probe on CpuAddress[1:0]
  Decoder decoder_1 (.out0(enableSet0), .out1(enableSet1), .sel(CpuAddress[2]));  // open: en
  SetLine setline_1 (
    .Tag(CpuAddress[9:3]), .clk(CLK), .enable(enableSet0), .offset(CpuAddress[1:0]), .Setvalid(valid),
    .contains(DidContain), .setBlock(CpuWriteValue));
  SetLine setline_2 (
    .Tag(CpuAddress[9:3]), .clk(CLK), .enable(enableSet1), .offset(CpuAddress[1:0]), .Setvalid(valid),
    .contains(DidContain), .setBlock(CpuWriteValue));
  fsm_controls fsm_controls_1 (
    .CLK(CLK), .r(CpuRead), .w(CpuWrite), .contains(DidContain), .ready(Ready), .setDirty(setDirty),
    .valid(setValid), .updateAge(updateAge), .memRead(MemRead), .memWrite(MemWrite));  // open: dirty, byteRead

  // Other names for the same wires on the sheet: SetNum = CpuAddress[2]; offset[1:0] = CpuAddress[1:0];
  //   TAG[6:0] = CpuAddress[9:3]

  // Notes on the sheet:
  //   Address Bits = 10
  //   Line Size = 4
  //   W = 3
  //   Num Sets = 2
  //   C =4*3*2 = 24bytes
  //   Tag bits = 7
endmodule

module Inputs (
  input  HaltTesting,
  input  Ready,
  input  CLK,
  output Done,
  output Read,
  output Write,
  output [9:0] Address,
  output [7:0] Value,
  output [9:0] TestNumber
);

  wire and_1_out, not_1_out, not_2_out;

  not not_1 (not_1_out, HaltTesting);
  not not_2 (not_2_out, Done);
  Counter #(.width(10), .max('h3ff), .ongoal("stay")) u_TestNumber (
    .count(and_1_out), .Q(TestNumber), .clk(CLK));  // open: load, D, carry, clr
  and and_1 (and_1_out, not_1_out, Ready, not_2_out);
  ROM #(.addrWidth(10), .dataWidth(21)) rom_1 (
    .addr(TestNumber), .data({Done, Read, Write, Address, Value}));  // open: sel

  // Notes on the sheet:
  //   contents of rom_1 (hex, n*v repeats v):
  //   40005 40106 40307 40308 41009 4110a 4130b 4130c 4200d 4210e 4230f 42310 43011 43112 43313 43314
  //   44015 44116 44317 44318 45019 4511a 4531b 4531c 80000 80100 80300 80300 81000 81100 81300 81300
  //   82000 82100 82300 82300 83000 83100 83300 83300 84000 84100 84300 84300 85000 85100 85300 85300 0
  //   100000
endmodule

module Checker (
  input  [9:0] TestNumber,
  input  [7:0] YourByteRead,
  output CmdIsRead,
  output [7:0] CorrectByteRead,
  output Correct
);

  wire comparator_1_eq;
  wire [9:0] subtractor_1_out;

  // Probe on TestNumber
  Subtractor #(.width(10)) subtractor_1 (.a(TestNumber), .b(10'h1), .out(subtractor_1_out));  // open: bin, bout
  ROM #(.addrWidth(10), .dataWidth(9)) rom_1 (
    .addr(subtractor_1_out), .data({CmdIsRead, CorrectByteRead}));  // open: sel
  Comparator #(.mode("unsigned")) comparator_1 (
    .a(YourByteRead), .b(CorrectByteRead), .eq(comparator_1_eq));  // open: gt, lt
  and and_1 (Correct, comparator_1_eq, CmdIsRead);

  // Other names for the same wires on the sheet: Test_Number[9:0] = TestNumber

  // Notes on the sheet:
  //   Read Solutions
  //   contents of rom_1 (hex, n*v repeats v):
  //   5 6 7 8 9 a b c d e f 10 11 12 13 14 15 16 17 18 19 1a 1b 1c 105 106 108 108 109 10a 10c 10c 10d 10e
  //   110 110 111 112 114 114 115 116 118 118 119 11a 11c 11c
endmodule

module SetLine (
  input  [6:0] Tag,
  input  clk,
  input  enable,
  input  [1:0] offset,
  input  Setvalid,
  input  [7:0] setBlock,
  output contains
);

  wire A, B, comparator_3_eq, comparator_4_eq, comparator_5_eq, dirty0, dirty1, dirty2, enable0, enable1,
       enable2, setDirty, valid0, valid1, valid2;
  wire [1:0] Age0, Age1, Age2, line_hit, LRU, multiplexer_1_out, multiplexer_3_out, updateAge;
  wire [2:0] and_1_out;
  wire [6:0] Tag0, Tag1, Tag2;
  wire [7:0] block0, block1, block2;

  Decoder #(.select(2)) decoder_1 (
    .out0(enable0), .out1(enable1), .out2(enable2), .sel(multiplexer_1_out), .en(enable));  // open: out3
  Multiplexer #(.width(2), .enable("false")) multiplexer_1 (
    .in0(LRU), .in1(line_hit), .out(multiplexer_1_out), .sel(contains));
  Line Set0 (
    .setTag(Tag), .setDirty(setDirty), .setAge(updateAge), .setValid(Setvalid), .offset(offset), .CLK(clk),
    .enable(enable0), .Block(block0), .Tag(Tag0), .Age(Age0), .dirty(dirty0), .valid(valid0),
    .SetData(setBlock));
  Comparator #(.width(2), .mode("unsigned")) comparator_1 (.a(Age0), .b(Age1), .lt(A));  // open: gt, eq
  // Probe on LRU
  Multiplexer #(.select(2), .width(2), .enable("false")) multiplexer_2 (
    .in0(2'b00), .in1(2'b01), .in2(2'b10), .in3(2'b10), .out(LRU), .sel({B, A}));
  Multiplexer #(.width(2), .enable("false")) multiplexer_3 (.in0(Age0), .in1(Age1), .out(multiplexer_3_out), .sel(A));
  Line Set1 (
    .setTag(Tag), .setDirty(setDirty), .setAge(updateAge), .setValid(Setvalid), .offset(offset), .CLK(clk),
    .enable(enable1), .Block(block1), .Tag(Tag1), .Age(Age1), .dirty(dirty1), .valid(valid1),
    .SetData(setBlock));
  Comparator #(.width(2), .mode("unsigned")) comparator_2 (.a(multiplexer_3_out), .b(Age2), .lt(B));  // open: gt, eq
  Line Set2 (
    .setTag(Tag), .setDirty(setDirty), .setAge(updateAge), .setValid(Setvalid), .offset(offset), .CLK(clk),
    .enable(enable2), .Block(block2), .Tag(Tag2), .Age(Age2), .dirty(dirty2), .valid(valid2),
    .SetData(setBlock));
  Comparator #(.width(7), .mode("unsigned")) comparator_3 (.a(Tag), .b(Tag0), .eq(comparator_3_eq));  // open: gt, lt
  Comparator #(.width(7), .mode("unsigned")) comparator_4 (.a(Tag), .b(Tag1), .eq(comparator_4_eq));  // open: gt, lt
  Comparator #(.width(7), .mode("unsigned")) comparator_5 (.a(Tag), .b(Tag2), .eq(comparator_5_eq));  // open: gt, lt
  and and_1 (and_1_out[0], comparator_3_eq, valid0);
  and and_2 (and_1_out[1], comparator_4_eq, valid1);
  and and_3 (and_1_out[2], comparator_5_eq, valid2);
  Multiplexer #(.select(3), .width(2), .enable("false")) multiplexer_4 (
    .in1(2'b00), .in2(2'b01), .in4(2'b10), .out(line_hit), .sel(and_1_out));  // open: in0, in3, in5, in6, in7
  or or_1 (contains, and_1_out[0], and_1_out[1], and_1_out[2]);

  // Other names for the same wires on the sheet: Data[7:0] = setBlock
endmodule

module Line (
  input  [6:0] setTag,
  input  setDirty,
  input  [1:0] setAge,
  input  setValid,
  input  [1:0] offset,
  input  CLK,
  input  [7:0] SetData,
  input  enable,
  output [7:0] Block,
  output [6:0] Tag,
  output [1:0] Age,
  output dirty,
  output valid
);

  wire decoder_1_out0, decoder_1_out1, decoder_1_out2, decoder_1_out3;
  wire [7:0] block_0, block_1, block_2, block_3;

  Decoder #(.select(2)) decoder_1 (
    .out0(decoder_1_out0), .out1(decoder_1_out1), .out2(decoder_1_out2), .out3(decoder_1_out3), .sel(offset),
    .en(enable));
  Register State (.D(SetData), .en(decoder_1_out0), .Q(block_0), .clk(CLK));  // open: clr
  Register State_2 (.D(SetData), .en(decoder_1_out1), .Q(block_1), .clk(CLK));  // open: clr
  Register State_3 (.D(SetData), .en(decoder_1_out2), .Q(block_2), .clk(CLK));  // open: clr
  Register State_4 (.D(SetData), .en(decoder_1_out3), .Q(block_3), .clk(CLK));  // open: clr
  Register #(.width(7)) State_5 (.D(setTag), .Q(Tag), .clk(CLK));  // open: en, clr
  Multiplexer #(.select(2), .width(8), .enable("false")) multiplexer_1 (
    .in0(block_0), .in1(block_1), .in2(block_2), .in3(block_3), .out(Block), .sel(offset));
  Register #(.width(2)) State_6 (.D(setAge), .Q(Age), .clk(CLK));  // open: en, clr
  Register #(.width(1)) State_7 (.D(setDirty), .Q(dirty), .clk(CLK));  // open: en, clr
  Register #(.width(1)) State_8 (.D(setValid), .Q(valid), .clk(CLK));  // open: en, clr

  // Other names for the same wires on the sheet: Age_t[1:0] = setAge; Data[7:0] = SetData; Tag_t[6:0] = setTag;
  //   valid_t = setValid
endmodule

module UpdateAge (
  input  [1:0] selectAge,
  input  [1:0] Age,
  output [1:0] nextAge
);

  wire [1:0] adder_1_out;
  wire [2:0] select;

  Comparator #(.width(2), .mode("unsigned")) comparator_1 (
    .a(Age), .b(selectAge), .gt(select[0]), .eq(select[1]), .lt(select[2]));
  // Probe on select
  Adder #(.width(2)) adder_1 (.a(Age), .b(2'b11), .out(adder_1_out));  // open: cin, cout
  Multiplexer #(.select(3), .width(2), .enable("false")) multiplexer_1 (
    .in1(Age), .in2(2'b00), .in4(adder_1_out), .out(nextAge), .sel(select));  // open: in0, in3, in5, in6, in7

  // Other names for the same wires on the sheet: selectedAge[1:0] = selectAge
endmodule

module fsm_controls (
  input  CLK,
  input  r,
  input  w,
  input  contains,
  input  dirty,
  output ready,
  output setDirty,
  output valid,
  output updateAge,
  output memRead,
  output memWrite,
  output byteRead
);

  wire A, and_1_out, and_2_out, and_3_out, and_4_out, and_5_out, and_6_out, and_7_out, and_8_out, and_9_out,
       and_10_out, and_11_out, and_12_out, and_13_out, and_14_out, and_15_out, and_16_out, and_17_out,
       and_18_out, B, C, not_1_out, not_2_out, not_3_out, not_4_out, not_5_out, not_6_out, not_7_out,
       not_8_out, not_9_out, not_10_out, not_11_out, not_12_out, not_13_out, not_14_out, not_15_out,
       not_16_out, not_17_out, not_18_out, not_19_out, not_20_out, not_21_out, not_22_out, not_23_out,
       not_24_out, not_25_out, not_26_out, not_27_out, not_28_out, not_29_out, not_30_out, not_31_out,
       not_32_out, not_33_out, not_34_out, not_35_out, not_36_out, not_37_out, not_38_out, not_39_out,
       not_40_out, or_1_out, or_2_out, or_3_out;

  not not_1 (not_1_out, A);
  not not_2 (not_2_out, C);
  not not_3 (not_3_out, contains);
  not not_4 (not_4_out, A);
  not not_5 (not_5_out, r);
  not not_6 (not_6_out, contains);
  not not_7 (not_7_out, r);
  not not_8 (not_8_out, dirty);
  not not_9 (not_9_out, A);
  not not_10 (not_10_out, r);
  not not_11 (not_11_out, w);
  not not_12 (not_12_out, A);
  not not_13 (not_13_out, contains);
  not not_14 (not_14_out, A);
  not not_15 (not_15_out, dirty);
  not not_16 (not_16_out, A);
  not not_17 (not_17_out, A);
  not not_18 (not_18_out, C);
  not not_19 (not_19_out, C);
  not not_20 (not_20_out, C);
  not not_21 (not_21_out, B);
  not not_22 (not_22_out, C);
  not not_23 (not_23_out, B);
  not not_24 (not_24_out, C);
  not not_25 (not_25_out, w);
  not not_26 (not_26_out, C);
  not not_27 (not_27_out, A);
  not not_28 (not_28_out, B);
  not not_29 (not_29_out, C);
  not not_30 (not_30_out, B);
  not not_31 (not_31_out, C);
  not not_32 (not_32_out, A);
  not not_33 (not_33_out, B);
  not not_34 (not_34_out, C);
  not not_35 (not_35_out, B);
  not not_36 (not_36_out, C);
  and and_1 (and_1_out, not_1_out, B, not_2_out, not_3_out);
  and and_2 (and_2_out, not_4_out, B, not_5_out, w, not_6_out);
  and and_3 (and_3_out, B, C, not_7_out, w, not_8_out);
  and and_4 (and_4_out, A, C);
  not not_37 (not_37_out, A);
  not not_38 (not_38_out, B);
  and and_5 (and_5_out, not_37_out, not_38_out, C);
  and and_6 (and_6_out, not_9_out, C, not_10_out, not_11_out);
  and and_7 (and_7_out, not_12_out, C, w, not_13_out);
  and and_8 (and_8_out, not_14_out, C, w, not_15_out);
  and and_9 (and_9_out, not_16_out, C, r, w);
  and and_10 (and_10_out, not_17_out, B, not_18_out, contains);
  and and_11 (and_11_out, A, not_39_out, not_40_out);
  not not_39 (not_39_out, B);
  not not_40 (not_40_out, C);
  and and_12 (and_12_out, not_19_out, dirty);
  and and_13 (and_13_out, not_20_out, contains);
  and and_14 (and_14_out, not_21_out, not_22_out, w);
  and and_15 (and_15_out, not_23_out, not_24_out, r);
  and and_16 (and_16_out, B, C, not_25_out);
  and and_17 (and_17_out, B, C, r);
  and and_18 (and_18_out, A, not_26_out);
  and and_19 (ready, not_27_out, not_28_out, C);
  and and_20 (setDirty, A, B, not_29_out);
  and and_21 (valid, A, not_30_out, not_31_out);
  and and_22 (updateAge, not_32_out, B, C);
  and and_23 (memRead, A, not_33_out, not_34_out);
  and and_24 (memWrite, A, not_35_out, C);
  and and_25 (byteRead, A, B, not_36_out);
  or or_1 (or_1_out, and_1_out, and_2_out, and_3_out, and_4_out);
  or or_2 (or_2_out, and_12_out, and_13_out, and_14_out, and_15_out, and_16_out, and_17_out, and_18_out);
  D_Flip_Flop d_ff_1 (.clk(CLK), .D(or_1_out), .Q(A));  // open: Qn, preset, en, reset
  or or_3 (or_3_out, and_5_out, and_6_out, and_7_out, and_8_out, and_9_out, and_10_out, and_11_out);
  D_Flip_Flop d_ff_2 (.clk(CLK), .D(or_2_out), .Q(C));  // open: Qn, preset, en, reset
  D_Flip_Flop d_ff_3 (.clk(CLK), .D(or_3_out), .Q(B));  // open: Qn, preset, en, reset
endmodule
